// Logisim project ALU.circ as structural Verilog
module ALU (
  input  [31:0] in_1,
  input  [2:0] select_Alu,
  input  [31:0] in_3,
  input  [31:0] in_4,
  output [31:0] Alu_Result,
  output Zero_Flag
);

  wire and_1_out, and_2_out, and_3_out, comparator_1_eq, comparator_1_gt, comparator_1_lt, comparator_2_eq,
       comparator_2_gt, comparator_2_lt, not_1_out, not_2_out, not_3_out, not_4_out;
  wire [31:0] bit_extender_1_out, bit_extender_2_out, shifter_1_out, shifter_2_out, shifter_3_out,
       shifter_4_out;

  Shifter #(.width(32)) shifter_1 (.in(in_3), .\dist (in_4[4:0]), .out(shifter_1_out));
  Shifter #(.width(32), .shift("lr")) shifter_2 (.in(in_3), .\dist (in_4[4:0]), .out(shifter_2_out));
  Shifter #(.width(32), .shift("ar")) shifter_3 (.in(in_3), .\dist (in_4[4:0]), .out(shifter_3_out));
  Shifter #(.width(32), .shift("ar")) shifter_4 (.in(in_3), .\dist (in_4[4:0]), .out(shifter_4_out));
  Comparator #(.width(32), .mode("unsigned")) comparator_1 (
    .a(in_3), .b({in_4[31:7], in_3[6], in_4[5:0]}), .gt(comparator_1_gt), .eq(comparator_1_eq),
    .lt(comparator_1_lt));
  Comparator #(.width(32)) comparator_2 (
    .a(in_3), .b({in_4[31:7], in_3[6], in_4[5:0]}), .gt(comparator_2_gt), .eq(comparator_2_eq),
    .lt(comparator_2_lt));
  not not_1 (not_1_out, comparator_1_gt);
  not not_2 (not_2_out, comparator_1_eq);
  not not_3 (not_3_out, comparator_2_gt);
  not not_4 (not_4_out, comparator_2_eq);
  and and_1 (and_1_out, not_1_out, not_2_out, comparator_1_lt);
  and and_2 (and_2_out, not_3_out, not_4_out, comparator_2_lt);
  and and_3 (and_3_out, in_1[0], in_1[1], in_1[2], in_1[3], in_1[4], in_1[5], in_1[6], in_1[7], in_1[8], in_1[9], in_1[10], in_1[11], in_1[12], in_1[14], in_1[14], in_1[15], in_1[16], in_1[17], in_1[18], in_1[19], in_1[20], in_1[21], in_1[22], in_1[23], in_1[24], in_1[25], in_1[26], in_1[27], in_1[28], in_1[29], in_1[30], in_1[31]);
  assign bit_extender_1_out = {{31{and_1_out}}, and_1_out};  // Bit_Extender bit_extender_1
  assign bit_extender_2_out = {{31{1'b0}}, and_2_out};  // Bit_Extender bit_extender_2
  not not_5 (Zero_Flag, and_3_out);
  Multiplexer #(.select(3), .width(32)) multiplexer_1 (
    .in0({in_1[31:14], in_1[14], in_1[12:0]}), .in1(shifter_1_out), .in2(shifter_2_out), .in3(shifter_3_out),
    .in4(shifter_4_out), .in5(bit_extender_1_out), .in6(bit_extender_2_out), .out(Alu_Result),
    .sel(select_Alu));  // open: in7, en

  assign in_1[13] = in_1[14];
  assign in_4[6] = in_3[6];

  // Other names for the same wires on the sheet: A[31:0] = in_3; A0 = in_3[0]; A1 = in_3[1]; A2 = in_3[2];
  //   A3 = in_3[3]; A4 = in_3[4]; A5 = in_3[5]; A7 = in_3[7]; A8 = in_3[8]; A9 = in_3[9]; A10 = in_3[10];
  //   A11 = in_3[11]; A12 = in_3[12]; A13 = in_3[13]; A14 = in_3[14]; A15 = in_3[15]; A16 = in_3[16]; A17 = in_3[17];
  //   A18 = in_3[18]; A19 = in_3[19]; A20 = in_3[20]; A21 = in_3[21]; A22 = in_3[22]; A23 = in_3[23]; A24 = in_3[24];
  //   A25 = in_3[25]; A26 = in_3[26]; A27 = in_3[27]; A28 = in_3[28]; A29 = in_3[29]; A30 = in_3[30]; A31 = in_3[31];
  //   B[31:0] = {in_4[31:7], in_3[6], in_4[5:0]}; B0 = in_4[0]; least_significant_5_bits_of_B[4:0] = in_4[4:0];
  //   B1 = in_4[1]; B2 = in_4[2]; B3 = in_4[3]; B4 = in_4[4]; B5 = in_4[5]; A6 = in_3[6]; B7 = in_4[7]; B8 = in_4[8];
  //   B9 = in_4[9]; B10 = in_4[10]; B11 = in_4[11]; B12 = in_4[12]; B13 = in_4[13]; B14 = in_4[14]; B15 = in_4[15];
  //   B16 = in_4[16]; B17 = in_4[17]; B18 = in_4[18]; B19 = in_4[19]; B20 = in_4[20]; B21 = in_4[21]; B22 = in_4[22];
  //   B23 = in_4[23]; B24 = in_4[24]; B25 = in_4[25]; B26 = in_4[26]; B27 = in_4[27]; B28 = in_4[28]; B29 = in_4[29];
  //   B30 = in_4[30]; B31 = in_4[31]; Result[31:0] = {in_1[31:14], in_1[14], in_1[12:0]}; Rs1 = in_1[0];
  //   Rs2 = in_1[1]; Rs3 = in_1[2]; Rs4 = in_1[3]; Rs5 = in_1[4]; Rs6 = in_1[5]; Rs7 = in_1[6]; Rs8 = in_1[7];
  //   Rs9 = in_1[8]; Rs10 = in_1[9]; Rs11 = in_1[10]; Rs12 = in_1[11]; Rs13 = in_1[12]; Rs14 = in_1[14];
  //   Rs15 = in_1[15]; Rs16 = in_1[16]; Rs17 = in_1[17]; Rs18 = in_1[18]; Rs19 = in_1[19]; Rs20 = in_1[20];
  //   Rs21 = in_1[21]; Rs22 = in_1[22]; Rs23 = in_1[23]; Rs24 = in_1[24]; Rs25 = in_1[25]; Rs26 = in_1[26];
  //   Rs27 = in_1[27]; Rs28 = in_1[28]; Rs29 = in_1[29]; Rs30 = in_1[30]; Rs31 = in_1[31]
endmodule

module Alu_1_bit (
  input  A,
  input  B,
  input  CarryIn,
  input  BInvert,
  input  AInvert,
  input  [1:0] Operation,
  output Result
);

  wire adder_1_cout, adder_1_out, and_1_out, multiplexer_1_out, multiplexer_2_out, not_1_out, not_2_out,
       or_1_out, xor_1_out;

  not not_1 (not_1_out, A);
  not not_2 (not_2_out, B);
  Multiplexer multiplexer_1 (.in0(A), .in1(not_1_out), .out(multiplexer_1_out), .sel(AInvert));  // open: en
  Multiplexer multiplexer_2 (.in0(B), .in1(not_2_out), .out(multiplexer_2_out), .sel(BInvert));  // open: en
  and and_1 (and_1_out, multiplexer_1_out, multiplexer_2_out);
  or or_1 (or_1_out, multiplexer_1_out, multiplexer_2_out);
  xor xor_1 (xor_1_out, multiplexer_1_out, multiplexer_2_out);
  Adder #(.width(1)) adder_1 (
    .a(multiplexer_1_out), .b(multiplexer_2_out), .out(adder_1_out), .cin(CarryIn), .cout(adder_1_cout));
  // Probe on adder_1_cout
  Multiplexer #(.select(2)) multiplexer_3 (
    .in0(and_1_out), .in1(or_1_out), .in2(xor_1_out), .in3(adder_1_out), .out(Result), .sel(Operation));  // open: en
endmodule
