// Logisim project data_mem.circ as structural Verilog: 1 circuit, main circuit main
module main (
  input  [31:0] in_1,
  input  in_2,
  input  in_3,
  input  in_4,
  input  [31:0] in_5,
  output [31:0] memory_output
);

  // Probe on in_5
  // Probe on in_1[19:0]
  RAM #(.addrWidth(20), .dataWidth(32), .trigger("falling"), .databus("bibus")) ram_1 (
    .addr(in_1[19:0]), .we(in_2), .oe(in_3), .clk(in_4), .din(in_5), .dout(memory_output));

  // Notes on the sheet:
  //   Alu_Result
endmodule
