// Logisim project data_path.circ as structural Verilog: 1 circuit, main circuit main
module main (
  output [31:0] out_1,
  output [31:0] out_2,
  output [31:0] out_3,
  output [31:0] out_4,
  output [31:0] out_5,
  output [31:0] out_6,
  output [31:0] out_7,
  output [31:0] out_8,
  output [31:0] out_9,
  output [31:0] out_10,
  output [31:0] out_11,
  output [31:0] out_12,
  output [31:0] out_13,
  output [31:0] out_14,
  output [31:0] out_15,
  output [31:0] out_16,
  output [31:0] out_17,
  output [31:0] out_18,
  output [31:0] out_19,
  output [31:0] out_20,
  output [31:0] out_21,
  output [31:0] out_22,
  output [31:0] out_23,
  output [31:0] out_24,
  output [31:0] out_25,
  output [31:0] out_26,
  output [31:0] out_27,
  output [31:0] out_28,
  output [31:0] out_29,
  output [31:0] out_30,
  output [31:0] out_31,
  output [31:0] out_32,
  output [31:0] out_33,
  output out_34,
  output out_35
);

  wire BEQ, BGE, BGEU, BLT, BLTU, BNE, clock, Extop, Extop_Ex, JALR, jalr_EX, jalr_MEM, jalr_t, Kill, kill_t,
       LessFlagSigned, LessFlagUnsigned, main_10_mem_to_reg, main_10_memory_read, main_10_memory_write,
       main_10_regwrite, mem_to_reg, mem_to_reg_EX, mem_to_reg_MEM, mem_to_reg_WB, Memory_Write,
       Memory_Write_EX, Memory_Write_MEM, MemRead, MemRead_EX, MemRead_Ex_t, MemRead_MEM, or_1_out, or_2_out,
       pc_src, RegWrite, RegWrite_EX, RegWrite_Ex_t, RegWrite_MEM, RegWrite_WB, SSET, Stall, ZeroFlag;
  wire [1:0] ALUsrc;
  wire [4:0] ImmL, ImmL_Ex, ImmL_ID, multiplexer_4_out, RD_EX, Rd_WB, Rd_WB_EX, Rd_WB_MEM, Rd_WB_WB, Rs1_Ex,
       RS1_ID, Rs1_ID_t, Rs2_Ex, RS2_ID, Rs2_ID_t;
  wire [5:0] OP;
  wire [7:0] ALU_Op, ALU_Op_Ex;
  wire [10:0] Funct, ImmU, ImmU_Ex;
  wire [15:0] Imm16, Imm16_Ex, Imm16_ID;
  wire [19:0] pc, PC_ID, pc_inc, pc_inc_EX, pc_inc_Ex_t, pc_inc_ID, pc_inc_MEM;
  wire [31:0] ALU_Result, ALU_Result_EX, ALU_Result_MEM, ALU_Result_WB, bit_extender_1_out,
       bit_extender_2_out, bit_extender_3_out, bit_extender_4_out, BusA, BusA_Ex, BusB, BusB_EX, BusB_Ex_t,
       BusB_MEM, main_2_out_2, main_3_instruction_2, MEM_Data_EX, MEM_Data_MEM, MEM_Data_WB,
       multiplexer_1_out, multiplexer_2_out, multiplexer_3_out, multiplexer_5_out, Write_Data;

  // pc_circut_main main_1: pin names not known; wires that end beside it: PC_ID, Stall, Imm16, Funct, ImmL_ID, BusA, clock, pc_src, jalr_t, pc_inc, pc
  // Probe on pc_inc
  // Probe on pc
  // Probe on pc
  Clock clock_1 (.out(clock));
  instruction_mem_main main_2 (.in_1(pc), .out_2(main_2_out_2));
  Multiplexer #(.width(32), .enable("false")) multiplexer_1 (
    .in0(main_2_out_2), .in1({32{1'b0}}), .out(multiplexer_1_out), .sel(kill_t));
  // Probe on Imm16
  // Probe on ImmL
  // Probe on ImmU
  IF_ID_REGISTER_main main_3 (
    .instruction(multiplexer_1_out), .PC_IF(pc), .pc_inc(pc_inc), .clk(clock), .stall(Stall),
    .instruction_2(main_3_instruction_2), .PC_ID(PC_ID), .pc_inc_2(pc_inc_ID));
  assign bit_extender_1_out = {{16{1'b0}}, Imm16};  // Bit_Extender bit_extender_1
  assign bit_extender_2_out = {{16{Imm16[15]}}, Imm16};  // Bit_Extender bit_extender_2
  assign bit_extender_3_out = {{16{ImmU[10]}}, {ImmU, ImmL}};  // Bit_Extender bit_extender_3
  Multiplexer #(.width(32), .enable("false")) multiplexer_2 (
    .in0(bit_extender_1_out), .in1(bit_extender_2_out), .out(multiplexer_2_out), .sel(Extop));
  or or_1 (or_1_out, BEQ, BNE, BLT, BLTU, BGE, BGEU);
  // Fetch_instruction_main main_4: pin names not known; wires that end beside it: Imm16_ID, Rs1_ID_t, Rs2_ID_t, main_3_instruction_2, ImmL_ID, OP, Funct
  Multiplexer #(.select(2), .width(32), .enable("false")) multiplexer_3 (
    .in0(BusB), .in1(multiplexer_2_out), .in2(bit_extender_3_out), .out(multiplexer_3_out), .sel(ALUsrc));  // open: in3
  // Probe on ALU_Op[5:4]
  // Probe on Rs1_ID_t
  // ALU_Full alu_full_1: pin names not known; wires that end beside it: BusA, multiplexer_3_out, ALU_Op[5:4], ALU_Op[7], ALU_Op[6], ALU_Op[6], ALU_Op[3:0], ALU_Result, LessFlagUnsigned, LessFlagSigned, out_34, out_35, ZeroFlag
  Multiplexer #(.width(5), .enable("false")) multiplexer_4 (
    .in0(Rs1_ID_t), .in1(Rd_WB), .out(multiplexer_4_out), .sel(SSET));
  // Probe on ALU_Result
  EX_MEM_Register_main main_5 (
    .BusB_EX(BusB_EX), .MemRead_EX(MemRead_EX), .MemWrite_EX(Memory_Write_EX), .MemtoReg_EX(mem_to_reg_EX),
    .RegWrite_EX(RegWrite_EX), .BusB_MEM(BusB_MEM), .MemRead_MEM(MemRead_MEM),
    .MemWrite_MEM(Memory_Write_MEM), .MemtoReg_MEM(mem_to_reg_MEM), .RegWrite_MEM(RegWrite_MEM),
    .ALU_result_MEM(ALU_Result_MEM), .Reg_Des_EX(Rd_WB_EX), .Reg_Des_MEM(Rd_WB_MEM), .in_1(clock),
    .ALU_result_EX(ALU_Result_EX), .pc_inc_EX(pc_inc_EX), .pc_inc_MEM(pc_inc_MEM), .jalr_EX(jalr_EX),
    .jalr_MEM(jalr_MEM));
  HazardDetection_main main_6 (
    .MemRead_EX(MemRead_Ex_t), .Branch(or_1_out), .jalr(JALR), .Kill(Kill), .Stall(Stall), .RS1_ID(RS1_ID),
    .RD_EX(RD_EX), .RS2_ID(RS2_ID));  // open: RD_WB, reg_Write_WB
  // Probe on Write_Data
  // Probe on OP
  // Probe on ALU_Result_MEM
  Reg_file reg_file_1 (
    .out_7(out_1), .out_19(BusA), .out_28(BusB), .RW(Rd_WB), .Reg_Write(RegWrite), .DATA_IN(Write_Data),
    .clock(clock), .BusB(Rs2_ID_t), .BusA(multiplexer_4_out), .out_9(out_4), .out_11(out_9), .out_14(out_13),
    .out_15(out_17), .out_16(out_19), .out_17(out_23), .out_18(out_21), .out_20(out_27), .out_21(out_25),
    .out_22(out_31), .out_23(out_29), .out_24(out_3), .out_25(out_33), .out_26(out_7), .out_29(out_12),
    .out_27(out_5), .out_30(out_10), .out_32(out_16), .out_31(out_14), .out_34(out_20), .out_33(out_18),
    .out_37(out_28), .out_39(out_32), .out_36(out_22), .out_35(out_24), .out_38(out_26), .out_40(out_30),
    .out_8(out_2), .out_10(out_6), .out_12(out_11), .out_13(out_15));
  // Probe on BusB
  data_mem_main main_7 (
    .in_1(ALU_Result_MEM), .in_2(Memory_Write_MEM), .in_3(MemRead_MEM), .in_4(clock),
    .memory_output(MEM_Data_EX), .in_5(BusB_MEM));
  // ID_EX_Reg_main main_8: pin names not known; wires that end beside it: pc_inc_ID, Rs1_ID_t, Rs2_ID_t, Rd_WB, BusA, BusB, RegWrite, Imm16, ImmL, ImmU, Extop, ALUsrc, ALU_Op, MemRead, Memory_Write, mem_to_reg, jalr_t, clock, pc_inc_Ex_t, Rs1_Ex, Rs2_Ex, Rd_WB, BusA_Ex, BusB_Ex_t, RegWrite_Ex_t, Imm16_Ex, ImmL_Ex, ImmU_Ex, Extop_Ex, ALUsrc, ALU_Op_Ex, MemRead, Memory_Write, mem_to_reg, jalr_EX
  MEM_WB_Register_main main_9 (
    .in_1(clock), .ALU_result_MEM(ALU_Result_MEM), .RegWrite_MEM(RegWrite_MEM), .RegWrite_WB(RegWrite_WB),
    .ALU_result_WB(ALU_Result_WB), .Reg_Des_MEM(Rd_WB_MEM), .MEM_Data_MEM(MEM_Data_MEM),
    .Reg_Des_WB(Rd_WB_WB), .MEM_Data_WB(MEM_Data_WB), .MemtoReg_MEM(mem_to_reg_MEM),
    .MemtoReg_WB(mem_to_reg_WB), .pc_inc_MEM(pc_inc_MEM), .pc_inc_WB(pc_inc_MEM), .jalr_MEM(jalr_MEM),
    .jalr_WB(jalr_MEM));
  MainControlUnit_main main_10 (
    .ALU_Op(ALU_Op), .mem_to_reg(main_10_mem_to_reg), .Memory_Read(main_10_memory_read),
    .Memory_Write(main_10_memory_write), .RegWrite(main_10_regwrite), .in_1(Funct), .Extop(Extop),
    .ALUsrc(ALUsrc), .in_2(OP), .SSET(SSET), .jalr(jalr_t), .Pc_src(pc_src), .ZeroFlag(ZeroFlag),
    .LessFlagSigned(LessFlagSigned), .LessFlagUnsigned(LessFlagUnsigned));
  // Probe on ALU_Result_WB
  Multiplexer #(.width(32), .enable("false")) multiplexer_5 (
    .in0(ALU_Result_WB), .out(multiplexer_5_out), .sel(mem_to_reg_WB));  // open: in1
  assign bit_extender_4_out = {{12{1'b0}}, pc_inc_MEM};  // Bit_Extender bit_extender_4
  Multiplexer #(.enable("false")) multiplexer_6 (
    .in0(main_10_mem_to_reg), .in1(1'b0), .out(mem_to_reg), .sel(or_2_out));
  Multiplexer #(.enable("false")) multiplexer_7 (.in0(main_10_memory_read), .in1(1'b0), .out(MemRead), .sel(or_2_out));
  Multiplexer #(.enable("false")) multiplexer_8 (
    .in0(main_10_memory_write), .in1(1'b0), .out(Memory_Write), .sel(or_2_out));
  Multiplexer #(.enable("false")) multiplexer_9 (.in0(main_10_regwrite), .in1(1'b0), .out(RegWrite), .sel(or_2_out));
  Multiplexer #(.width(32), .enable("false")) multiplexer_10 (
    .in0(multiplexer_5_out), .in1(bit_extender_4_out), .out(Write_Data), .sel(jalr_MEM));
  or or_2 (or_2_out, Kill, Stall);

  assign out_8 = out_7;

  // Other names for the same wires on the sheet: ImmU_ID[10:0] = Funct; R0[31:0] = out_1; R1[31:0] = out_2;
  //   R2[31:0] = out_4; R3[31:0] = out_6; R4[31:0] = out_9; R5[31:0] = out_11; R6[31:0] = out_13; R7[31:0] = out_15;
  //   R8[31:0] = out_17; R9[31:0] = out_19; R10[31:0] = out_21; R11[31:0] = out_23; R12[31:0] = out_25;
  //   R13[31:0] = out_27; R14[31:0] = out_29; R15[31:0] = out_31; R16[31:0] = out_33; R17[31:0] = out_3;
  //   R18[31:0] = out_5; R19[31:0] = out_7; R20[31:0] = out_10; R21[31:0] = out_12; R22[31:0] = out_14;
  //   R23[31:0] = out_16; R24[31:0] = out_18; R25[31:0] = out_20; R26[31:0] = out_22; R27[31:0] = out_24;
  //   R28[31:0] = out_26; R29[31:0] = out_28; R30[31:0] = out_30; R31[31:0] = out_32; Rd_ID[4:0] = ImmL_ID

  // Notes on the sheet:
  //   Registers
  //   IF
  //   EX
  //   signal
  //   ID
  //   MEM
  //   WB
endmodule
