// Logisim project instruction_mem.circ as structural Verilog: 1 circuit, main circuit main
module main (
);

  wire [19:0] pc;
  wire [31:0] rom_1_data;

  ROM #(.addrWidth(20), .dataWidth(32)) rom_1 (.addr(pc), .data(rom_1_data));
endmodule
